// Digital circuit S-L-O.dig as structural Verilog
module S_L_O (
  input  iR,
  input  iG,
  input  Ck,
  output R,
  output Y,
  output G
);

  wire and_1_out, and_2_out, and_3_out, d_ff_1_nq, d_ff_1_q, d_ff_2_nq, d_ff_2_q, nand_1_out, nand_2_out,
       not_1_out, not_2_out, or_1_out;

  not not_1 (not_1_out, iG);
  not not_2 (not_2_out, iR);
  or or_1 (or_1_out, iR, not_1_out);
  nand nand_1 (nand_1_out, R, or_1_out);
  nand nand_2 (nand_2_out, iG, not_2_out, G);
  and and_1 (and_1_out, Ck, nand_1_out, nand_2_out);
  D_FF d_ff_1 (.D(and_2_out), .C(and_1_out), .Q(d_ff_1_q), .nQ(d_ff_1_nq));
  D_FF d_ff_2 (.D(and_3_out), .C(and_1_out), .Q(d_ff_2_q), .nQ(d_ff_2_nq));
  and and_2 (and_2_out, d_ff_1_nq, d_ff_2_q);
  and and_3 (and_3_out, d_ff_1_nq, d_ff_2_nq);
  and and_4 (R, d_ff_1_q, d_ff_2_nq);
  and and_5 (Y, d_ff_1_nq, d_ff_2_q);
  and and_6 (G, d_ff_1_nq, d_ff_2_nq);
endmodule
