// Digital circuit Snorte.dig as structural Verilog
module Snorte (
  input  iR,
  input  Ck,
  input  iG,
  output R,
  output aG,
  output aY,
  output Y,
  output G,
  output oG
);

  wire and_1_out, and_2_out, and_3_out, and_4_out, D0_nq, D0_q, D1_nq, D1_q, D2_nq, D2_q, nand_1_out,
       nand_2_out, not_1_out, not_2_out, not_3_out, not_4_out, or_1_out, xor_1_out;

  not not_1 (not_1_out, aG);
  not not_2 (not_2_out, iR);
  nand nand_1 (nand_1_out, R, iR);
  or or_1 (or_1_out, iR, not_1_out, iG);
  nand nand_2 (nand_2_out, iG, not_2_out, oG);
  and and_1 (and_1_out, nand_1_out, or_1_out, Ck, nand_2_out);
  D_FF D2 (.D(and_2_out), .C(and_1_out), .Q(D2_q), .nQ(D2_nq));
  D_FF D1 (.D(and_4_out), .C(and_1_out), .Q(D1_q), .nQ(D1_nq));
  D_FF D0 (.D(and_3_out), .C(and_1_out), .Q(D0_q), .nQ(D0_nq));
  and and_2 (and_2_out, D2_nq, D1_q, D0_q);
  xor xor_1 (xor_1_out, D0_q, D1_q);
  and and_3 (and_3_out, D2_nq, D0_nq);
  and and_4 (and_4_out, xor_1_out, D2_nq);
  and and_5 (R, D2_nq, D1_nq, D0_nq);
  and and_6 (aG, D2_nq, D1_nq, D0_q);
  and and_7 (aY, D2_nq, D1_q, D0_nq);
  or or_2 (G, D0_q, D1_q);
  and and_8 (Y, D2_q, D1_nq, D0_nq);
  and and_9 (oG, not_4_out, not_3_out, G);
  not not_3 (not_3_out, aY);
  not not_4 (not_4_out, aG);
endmodule
