// Digital circuit Transito.dig as structural Verilog
module Transito (
  input  C,
  input  C_2,
  input  clk,
  input  P,
  output C_3
);

  wire and_1_out, or_1_out, or_2_out, or_3_out, or_4_out, s_l_o_1_g, s_l_o_1_r, s_l_o_1_y, s_l_o_2_g,
       s_l_o_2_r, s_l_o_2_y, s_l_o_3_g, s_l_o_3_r, s_l_o_3_y, snorte_1_ag, snorte_1_ay, snorte_1_g,
       snorte_1_og, snorte_1_r, snorte_1_y;

  or or_1 (or_1_out, P, C);
  S_L_O s_l_o_1 (.iR(or_1_out), .iG(snorte_1_r), .Ck(clk), .R(s_l_o_1_r), .Y(s_l_o_1_y), .G(s_l_o_1_g));
  LED led_1 (.in(s_l_o_1_r));
  LED led_2 (.in(s_l_o_1_y));
  LED led_3 (.in(s_l_o_1_g));
  LED led_4 (.in(and_1_out));
  and and_1 (and_1_out, s_l_o_1_r, s_l_o_2_r, snorte_1_r, s_l_o_3_r, P);
  or or_2 (or_2_out, P, C_2);
  LED led_5 (.in(snorte_1_r));
  LED led_6 (.in(snorte_1_y));
  LED led_7 (.in(snorte_1_g));
  Snorte snorte_1 (
    .iR(or_2_out), .Ck(clk), .iG(C), .R(snorte_1_r), .aG(snorte_1_ag), .aY(snorte_1_ay), .Y(snorte_1_y),
    .G(snorte_1_g), .oG(snorte_1_og));
  LED led_8 (.in(snorte_1_ay));
  LED led_9 (.in(snorte_1_ag));
  LED led_10 (.in(s_l_o_2_r));
  LED led_11 (.in(s_l_o_2_y));
  LED led_12 (.in(s_l_o_2_g));
  S_L_O s_l_o_2 (.iR(or_3_out), .iG(snorte_1_og), .Ck(clk), .R(s_l_o_2_r), .Y(s_l_o_2_y), .G(s_l_o_2_g));
  LED led_13 (.in(and_1_out));
  or or_3 (or_3_out, P, C_2);
  LED led_14 (.in(s_l_o_3_g));
  LED led_15 (.in(s_l_o_3_y));
  LED led_16 (.in(s_l_o_3_r));
  S_L_O s_l_o_3 (.iR(or_4_out), .iG(snorte_1_r), .Ck(clk), .R(s_l_o_3_r), .Y(s_l_o_3_y), .G(s_l_o_3_g));
  or or_4 (or_4_out, P, C);

  assign C_3 = C_2;
endmodule
